// Logisim project mod4down.circ as structural Verilog: 1 circuit, main circuit main
module main (
  output [1:0] out_1
);

  wire clock_1_out;
  wire [1:0] rom_1_data;

  ROM #(.addrWidth(2), .dataWidth(2)) rom_1 (.addr(out_1), .data(rom_1_data));  // open: sel
  Clock clock_1 (.out(clock_1_out));
  Register #(.width(2)) register_1 (.D(rom_1_data), .Q(out_1), .clk(clock_1_out));  // open: en, clr

  // Notes on the sheet:
  //   contents of rom_1 (hex, n*v repeats v):
  //   3 0 1 2
endmodule
